# Fritzing sketch wireless_gondola_wiring (saved by Fritzing 0.9.3b)

parts:
  Pen_lift_Servo = Basic Servo
  Bauteil1 = Adafruit HUZZAH32 ESP32 Feather [part_number="Adafruit #3405"]
  U1 = LIPO-2000mAh [package=lipo-2000]
  U2 = SWITCH_SPDT [package=kps-1290]

nets:
  GND: Pen_lift_Servo.gnd, Bauteil1.GND
  N1: Pen_lift_Servo.vcc, Bauteil1.VBAT
  N2: Pen_lift_Servo.pulse, Bauteil1.IO13_A12
  N3: U1.+, U2.O

notes:
  ...
