# Fritzing sketch drewie_wiring_a4988 (saved by Fritzing 0.9.4)

parts:
  Left_Motor = Stepper Motor - Bipolar
  Right_Motor = Stepper Motor - Bipolar
  J1 = Power Jack [package=power_jack_pth]
  Set_to_5V = LM2596 step down module
  Pololu_A2 = Pololu A4988 [package=SO16]
  Raspberry_Pi_1 = Raspberry Pi 3 [part_number=RPI-3-V1.2]
  U1 = SPDT Slide Switch [package=ayz0202]
  Pololu_A1 = Pololu A4988 [package=SO16]
  J2 = Basic Servo

nets (from the breadboard view):
  N1: Left_Motor.A, Pololu_A1.2B
  N2: Left_Motor.C, Pololu_A1.2A
  N3: Left_Motor.B, Pololu_A1.1A
  N4: Left_Motor.D, Pololu_A1.1B
  N5: Right_Motor.A, Pololu_A2.2B
  N6: Right_Motor.C, Pololu_A2.2A
  N7: Right_Motor.B, Pololu_A2.1A
  N8: Right_Motor.D, Pololu_A2.1B
  GND: J1.GND, Set_to_5V.IN-, Set_to_5V.OUT-, Pololu_A2.GND, Raspberry_Pi_1.GND, Pololu_A1.GND, J2.gnd
  N9: J1.PWR, Set_to_5V.IN+, U1.5
  5V: Set_to_5V.OUT+, Raspberry_Pi_1.5V, J2.vcc
  N10: Pololu_A2.MS1, Pololu_A2.MS2, Pololu_A2.VDD, Raspberry_Pi_1.GIPO20
  N11: Pololu_A2.RESET, Pololu_A2.SLEEP
  N12: Pololu_A2.STEP, Raspberry_Pi_1.GIPO19
  N13: Pololu_A2.DIR, Raspberry_Pi_1.GIPO6
  N14: Pololu_A2.VMOT, U1.6, Pololu_A1.VMOT
  N15: Raspberry_Pi_1.GIPO5, Pololu_A1.DIR
  N16: Raspberry_Pi_1.GIPO13, Pololu_A1.STEP
  N17: Raspberry_Pi_1.GIPO16, Pololu_A1.MS1, Pololu_A1.MS2, Pololu_A1.VDD
  N18: Pololu_A1.RESET, Pololu_A1.SLEEP

notes:
  Motorwiring has to be checked and testedindividually - different motors have different cable colors and setups

custom parts:
  LM2596 step down module: LM2596 DC-DC step down power supply module 3 A.
